# Fritzing sketch 05. fritzing-diagram-full (saved by Fritzing 0.9.3b)
breadboards: 1

parts:
  Εξάρτημα1 = Arduino Mega 2560 (Rev3)
  Εξάρτημα2 = Triple Axis Accelerometer Breakout - ADXL335
  Εξάρτημα3 = Triple Axis Accelerometer Breakout - ADXL335
  Εξάρτημα4 = Triple Axis Accelerometer Breakout - ADXL335
  Εξάρτημα5 = Triple Axis Accelerometer Breakout - ADXL335
  Εξάρτημα6 = Triple Axis Accelerometer Breakout - ADXL335
  Εξάρτημα7 = Triple Axis Accelerometer Breakout - ADXL335
  Εξάρτημα8 = Triple Axis Accelerometer Breakout - ADXL335
  Εξάρτημα9 = Triple Axis Accelerometer Breakout - ADXL335
  R1 = Resistor [tolerance=±5% resistance=220 package=THT]
  R2 = Resistor [tolerance=±5% resistance=220 package=THT]
  LED1 = RGB LED (com. cathode, rgb) [package="5 mm [THT]"]
  LED8 = RGB LED (com. cathode, rgb) [package="5 mm [THT]"]
  LED7 = RGB LED (com. cathode, rgb) [package="5 mm [THT]"]
  LED6 = RGB LED (com. cathode, rgb) [package="5 mm [THT]"]
  LED5 = RGB LED (com. cathode, rgb) [package="5 mm [THT]"]
  LED4 = RGB LED (com. cathode, rgb) [package="5 mm [THT]"]
  LED3 = RGB LED (com. cathode, rgb) [package="5 mm [THT]"]
  LED2 = RGB LED (com. cathode, rgb) [package="5 mm [THT]"]

nets:
  N1: Εξάρτημα1.A8, Εξάρτημα7.XOUT
  N2: Εξάρτημα1.A9, Εξάρτημα7.YOUT
  N3: Εξάρτημα1.A10, Εξάρτημα3.XOUT
  N4: Εξάρτημα1.A11, Εξάρτημα3.YOUT
  N5: Εξάρτημα1.A12, Εξάρτημα9.XOUT
  N6: Εξάρτημα1.A13, Εξάρτημα9.YOUT
  N7: Εξάρτημα1.A14, Εξάρτημα8.XOUT
  N8: Εξάρτημα1.A15, Εξάρτημα8.YOUT
  N9: Εξάρτημα1.A0, Εξάρτημα2.XOUT
  N10: Εξάρτημα1.A1, Εξάρτημα2.YOUT
  N11: Εξάρτημα1.A2, Εξάρτημα4.XOUT
  N12: Εξάρτημα1.A3, Εξάρτημα4.YOUT
  N13: Εξάρτημα1.A4, Εξάρτημα5.XOUT
  N14: Εξάρτημα1.A5, Εξάρτημα5.YOUT
  N15: Εξάρτημα1.A6, Εξάρτημα6.XOUT
  N16: Εξάρτημα1.A7, Εξάρτημα6.YOUT
  N17: Εξάρτημα1.3V3, R1.Pin_1, LED1.common_cathode, LED8.common_cathode, LED7.common_cathode, LED6.common_cathode, LED5.common_cathode, LED4.common_cathode, LED3.common_cathode, LED2.common_cathode
  VCC: Εξάρτημα1.5V, Εξάρτημα2.VCC, Εξάρτημα3.VCC, Εξάρτημα4.VCC, Εξάρτημα5.VCC, Εξάρτημα6.VCC, Εξάρτημα7.VCC, Εξάρτημα8.VCC, Εξάρτημα9.VCC
  N18: Εξάρτημα1.GND, R1.Pin_0, R2.Pin_1
  N19: Εξάρτημα1.D30, LED2.red_anode
  N20: Εξάρτημα1.D31, LED6.red_anode
  N21: Εξάρτημα1.D32, LED2.green_anode
  N22: Εξάρτημα1.D33, LED6.green_anode
  N23: Εξάρτημα1.D34, LED2.blue_anode
  N24: Εξάρτημα1.D35, LED6.blue_anode
  N25: Εξάρτημα1.D36, LED3.red_anode
  N26: Εξάρτημα1.D37, LED7.red_anode
  N27: Εξάρτημα1.D38, LED3.green_anode
  N28: Εξάρτημα1.D39, LED7.green_anode
  N29: Εξάρτημα1.D40, LED3.blue_anode
  N30: Εξάρτημα1.D41, LED7.blue_anode
  N31: Εξάρτημα1.D42, LED4.red_anode
  N32: Εξάρτημα1.D43, LED8.red_anode
  N33: Εξάρτημα1.D44, LED4.green_anode
  N34: Εξάρτημα1.D45, LED8.green_anode
  N35: Εξάρτημα1.D46, LED4.blue_anode
  N36: Εξάρτημα1.D47, LED8.blue_anode
  N37: Εξάρτημα1.D48, LED5.red_anode
  N38: Εξάρτημα1.D49, LED1.red_anode
  N39: Εξάρτημα1.D50, LED5.green_anode
  N40: Εξάρτημα1.D51, LED1.green_anode
  N41: Εξάρτημα1.D52, LED5.blue_anode
  N42: Εξάρτημα1.D53, LED1.blue_anode
  GND: Εξάρτημα2.GND, Εξάρτημα3.GND, Εξάρτημα4.GND, Εξάρτημα5.GND, Εξάρτημα6.GND, Εξάρτημα7.GND, Εξάρτημα8.GND, Εξάρτημα9.GND, R2.Pin_0

notes:
  The Chinese Seismograph
